# Fritzing sketch 05-03-sw-pd-event (saved by Fritzing 0.9.3b)
breadboards: 1

parts:
  S1 = Pushbutton [package="[THT]"]
  R1 = Resistor [tolerance=±5% resistance=220 package="0805 [SMD]"]
  Raspberry_Pi_1 = Raspberry Pi 3 [part_number=RPI-3-V1.2]
  R2 = Resistor [tolerance=±5% resistance=220 package="0805 [SMD]"]
  LED1 = LED - 5mm [color="Red (633nm)" package="5 mm [THT]"]

nets:
  N1: S1.Pin_1, S1.Pin_2, R1.Pin_0
  3V3: S1.Pin_3, S1.Pin_4, Raspberry_Pi_1.3v3, Raspberry_Pi_1.3V3
  N2: R1.Pin_1, Raspberry_Pi_1.GND, LED1.anode
  N3: Raspberry_Pi_1.GIPO25, R2.Pin_0
